// Logisim project main.circ as structural Verilog: 1 circuit, main circuit main
module main (
  input  in_1,
  input  in_2,
  input  in_3,
  output Output
);


  // Notes on the sheet:
  //   Inputs
endmodule
