// Logisim project subadder.circ as structural Verilog: 1 circuit, main circuit main
module main (
  input  sub_1__add_0,
  input  in_2,
  input  in_3,
  input  in_4,
  input  in_5,
  input  in_6,
  input  in_7,
  input  in_8,
  input  in_9,
  output out_10,
  output out_11,
  output out_12,
  output out_13
);

  wire adder_1_cout, adder_2_cout, adder_3_cout, adder_4_cout, multiplexer_1_out, multiplexer_2_out,
       multiplexer_3_out, multiplexer_4_out, not_1_out, not_2_out, not_3_out, not_4_out;

  Multiplexer #(.enable("false")) multiplexer_1 (
    .in0(in_3), .in1(not_1_out), .out(multiplexer_1_out), .sel(sub_1__add_0));
  not not_1 (not_1_out, in_3);
  Multiplexer #(.enable("false")) multiplexer_2 (
    .in0(in_5), .in1(not_2_out), .out(multiplexer_2_out), .sel(sub_1__add_0));
  not not_2 (not_2_out, in_5);
  Multiplexer #(.enable("false")) multiplexer_3 (
    .in0(in_7), .in1(not_3_out), .out(multiplexer_3_out), .sel(sub_1__add_0));
  not not_3 (not_3_out, in_7);
  Multiplexer #(.enable("false")) multiplexer_4 (
    .in0(in_9), .in1(not_4_out), .out(multiplexer_4_out), .sel(sub_1__add_0));
  not not_4 (not_4_out, in_9);
  Adder #(.width(1)) adder_1 (.a(in_2), .b(multiplexer_1_out), .out(out_10), .cin(sub_1__add_0), .cout(adder_1_cout));
  Adder #(.width(1)) adder_2 (.a(in_4), .b(multiplexer_2_out), .out(out_11), .cin(adder_1_cout), .cout(adder_2_cout));
  Adder #(.width(1)) adder_3 (.a(in_6), .b(multiplexer_3_out), .out(out_12), .cin(adder_2_cout), .cout(adder_3_cout));
  Adder #(.width(1)) adder_4 (.a(in_8), .b(multiplexer_4_out), .out(out_13), .cin(adder_3_cout), .cout(adder_4_cout));
endmodule
