// Logisim project test.circ as structural Verilog: 1 circuit, main circuit main
module main (
  input  in_1,
  input  in_2,
  input  in_3,
  input  in_4,
  output out_5
);

  wire A_prime_B_prime_CD_out, and_1_out, not_1_out, not_2_out, not_3_out, not_4_out;

  not not_1 (not_1_out, in_1);
  not not_2 (not_2_out, in_2);
  not not_3 (not_3_out, in_3);
  not not_4 (not_4_out, in_4);
  and and_1 (and_1_out, not_1_out, not_2_out, not_4_out);
  and A_prime_B_prime_CD (A_prime_B_prime_CD_out, not_1_out, not_2_out, in_4);
  or or_1 (out_5, A_prime_B_prime_CD_out, and_1_out);

  // Notes on the sheet:
  //   A'B'CD'
endmodule
